# Fritzing sketch Optical Synthesizer R2 (saved by Fritzing 0.9.3b)
perfboards: 3
stripboards: 4

parts:
  Part1 = Arduino Mega 2560 (Rev3)
  J2 = shrouded pin header, 26 pins [form="♂ (shrouded male)"]
  J3 = double row female pin header, 26 pins [form="♀ (female)"]
  Pressure_Sensing_Resistor = Basic Force Sensing Resistor (FSR) [package=THT]
  D1 = P1000K [part_number=P1000K]
  D2 = P1000K [part_number=P1000K]
  D3 = P1000K [part_number=P1000K]
  D4 = P1000K [part_number=P1000K]
  D5 = P1000K [part_number=P1000K]
  D6 = P1000K [part_number=P1000K]
  D7 = P1000K [part_number=P1000K]
  D8 = P1000K [part_number=P1000K]
  D9 = P1000K [part_number=P1000K]
  D10 = P1000K [part_number=P1000K]
  D11 = P1000K [part_number=P1000K]
  D12 = P1000K [part_number=P1000K]
  D13 = P1000K [part_number=P1000K]
  D14 = P1000K [part_number=P1000K]
  D15 = P1000K [part_number=P1000K]
  D16 = P1000K [part_number=P1000K]
  D17 = P1000K [part_number=P1000K]
  D18 = P1000K [part_number=P1000K]
  D19 = P1000K [part_number=P1000K]
  D20 = P1000K [part_number=P1000K]
  D21 = P1000K [part_number=P1000K]
  D22 = P1000K [part_number=P1000K]
  D23 = P1000K [part_number=P1000K]
  D24 = P1000K [part_number=P1000K]
  D25 = P1000K [part_number=P1000K]
  D26 = P1000K [part_number=P1000K]
  D27 = P1000K [part_number=P1000K]
  D28 = P1000K [part_number=P1000K]
  D29 = P1000K [part_number=P1000K]
  D30 = P1000K [part_number=P1000K]
  D31 = P1000K [part_number=P1000K]
  D32 = P1000K [part_number=P1000K]
  S9 = Pushbutton [package=THT]
  S10 = Pushbutton [package=THT]
  S11 = Pushbutton [package=THT]
  S12 = Pushbutton [package=THT]
  S13 = Pushbutton [package=THT]
  S14 = Pushbutton [package=THT]
  S15 = Pushbutton [package=THT]
  S16 = Pushbutton [package=THT]
  D33 = P1000K [part_number=P1000K]
  D34 = P1000K [part_number=P1000K]
  D35 = P1000K [part_number=P1000K]
  D36 = P1000K [part_number=P1000K]
  D37 = P1000K [part_number=P1000K]
  D38 = P1000K [part_number=P1000K]
  D39 = P1000K [part_number=P1000K]
  D40 = P1000K [part_number=P1000K]
  D41 = P1000K [part_number=P1000K]
  D42 = P1000K [part_number=P1000K]
  D43 = P1000K [part_number=P1000K]
  D44 = P1000K [part_number=P1000K]
  D45 = P1000K [part_number=P1000K]
  D46 = P1000K [part_number=P1000K]
  D47 = P1000K [part_number=P1000K]
  D48 = P1000K [part_number=P1000K]
  D49 = P1000K [part_number=P1000K]
  D50 = P1000K [part_number=P1000K]
  D51 = P1000K [part_number=P1000K]
  D52 = P1000K [part_number=P1000K]
  D53 = P1000K [part_number=P1000K]
  D54 = P1000K [part_number=P1000K]
  D55 = P1000K [part_number=P1000K]
  D56 = P1000K [part_number=P1000K]
  D57 = P1000K [part_number=P1000K]
  D58 = P1000K [part_number=P1000K]
  D59 = P1000K [part_number=P1000K]
  D60 = P1000K [part_number=P1000K]
  D61 = P1000K [part_number=P1000K]
  D62 = P1000K [part_number=P1000K]
  D63 = P1000K [part_number=P1000K]
  D64 = P1000K [part_number=P1000K]
  S17 = Pushbutton [package=THT]
  S18 = Pushbutton [package=THT]
  S19 = Pushbutton [package=THT]
  S20 = Pushbutton [package=THT]
  S21 = Pushbutton [package=THT]
  S22 = Pushbutton [package=THT]
  S23 = Pushbutton [package=THT]
  S24 = Pushbutton [package=THT]
  S25 = Pushbutton [package=THT]
  S26 = Pushbutton [package=THT]
  S27 = Pushbutton [package=THT]
  S28 = Pushbutton [package=THT]
  S29 = Pushbutton [package=THT]
  S30 = Pushbutton [package=THT]
  S31 = Pushbutton [package=THT]
  S32 = Pushbutton [package=THT]
  D65 = P1000K [part_number=P1000K]
  D66 = P1000K [part_number=P1000K]
  D67 = P1000K [part_number=P1000K]
  D68 = P1000K [part_number=P1000K]
  D69 = P1000K [part_number=P1000K]
  D70 = P1000K [part_number=P1000K]
  D71 = P1000K [part_number=P1000K]
  D73 = P1000K [part_number=P1000K]
  D74 = P1000K [part_number=P1000K]
  D75 = P1000K [part_number=P1000K]
  D76 = P1000K [part_number=P1000K]
  D77 = P1000K [part_number=P1000K]
  D78 = P1000K [part_number=P1000K]
  D79 = P1000K [part_number=P1000K]
  D80 = P1000K [part_number=P1000K]
  D81 = P1000K [part_number=P1000K]
  D82 = P1000K [part_number=P1000K]
  D83 = P1000K [part_number=P1000K]
  D84 = P1000K [part_number=P1000K]
  D85 = P1000K [part_number=P1000K]
  D86 = P1000K [part_number=P1000K]
  D87 = P1000K [part_number=P1000K]
  D88 = P1000K [part_number=P1000K]
  D89 = P1000K [part_number=P1000K]
  D90 = P1000K [part_number=P1000K]
  D91 = P1000K [part_number=P1000K]
  D92 = P1000K [part_number=P1000K]
  D94 = P1000K [part_number=P1000K]
  D95 = P1000K [part_number=P1000K]
  D96 = P1000K [part_number=P1000K]
  D97 = P1000K [part_number=P1000K]
  D98 = P1000K [part_number=P1000K]
  D99 = P1000K [part_number=P1000K]
  D100 = P1000K [part_number=P1000K]
  D102 = P1000K [part_number=P1000K]
  D103 = P1000K [part_number=P1000K]
  D105 = P1000K [part_number=P1000K]
  D106 = P1000K [part_number=P1000K]
  D107 = P1000K [part_number=P1000K]
  D108 = P1000K [part_number=P1000K]
  D110 = P1000K [part_number=P1000K]
  D111 = P1000K [part_number=P1000K]
  D112 = P1000K [part_number=P1000K]
  D113 = P1000K [part_number=P1000K]
  D114 = P1000K [part_number=P1000K]
  D115 = P1000K [part_number=P1000K]
  D116 = P1000K [part_number=P1000K]
  D117 = P1000K [part_number=P1000K]
  D118 = P1000K [part_number=P1000K]
  D119 = P1000K [part_number=P1000K]
  D120 = P1000K [part_number=P1000K]
  D121 = P1000K [part_number=P1000K]
  D122 = P1000K [part_number=P1000K]
  D124 = P1000K [part_number=P1000K]
  D125 = P1000K [part_number=P1000K]
  D126 = P1000K [part_number=P1000K]
  D127 = P1000K [part_number=P1000K]
  D128 = P1000K [part_number=P1000K]
  S33 = Pushbutton [package=THT]
  S34 = Pushbutton [package=THT]
  S36 = Pushbutton [package=THT]
  S37 = Pushbutton [package=THT]
  S38 = Pushbutton [package=THT]
  S39 = Pushbutton [package=THT]
  S40 = Pushbutton [package=THT]
  S42 = Pushbutton [package=THT]
  S43 = Pushbutton [package=THT]
  S44 = Pushbutton [package=THT]
  S46 = Pushbutton [package=THT]
  S47 = Pushbutton [package=THT]
  S48 = Pushbutton [package=THT]
  S49 = Pushbutton [package=THT]
  S50 = Pushbutton [package=THT]
  S51 = Pushbutton [package=THT]
  S52 = Pushbutton [package=THT]
  S53 = Pushbutton [package=THT]
  S54 = Pushbutton [package=THT]
  S55 = Pushbutton [package=THT]
  S56 = Pushbutton [package=THT]
  S57 = Pushbutton [package=THT]
  S58 = Pushbutton [package=THT]
  S59 = Pushbutton [package=THT]
  S60 = Pushbutton [package=THT]
  S61 = Pushbutton [package=THT]
  S62 = Pushbutton [package=THT]
  S63 = Pushbutton [package=THT]
  S64 = Pushbutton [package=THT]
  S7 = Pushbutton [package=THT]
  S6 = Pushbutton [package=THT]
  S1 = Pushbutton [package=THT]
  S8 = Pushbutton [package=THT]
  S2 = Pushbutton [package=THT]
  S5 = Pushbutton [package=THT]
  S4 = Pushbutton [package=THT]
  S3 = Pushbutton [package=THT]
  R2 = Resistor [tolerance=±5% resistance=220 package=THT]
  Slide_Pot = Slide Potentiometer [maximum_resistance=10kΩ]
  C1 = Capacitor Polarized [part_number=1000uf package=cpol-radial-1000uf-25v]
  Power_plug1 = Power plug
  MIDI_IN = DIN-5 jack (MIDI) [package=THT]
  7 = OPTO_DARL_6N138S [package=8-smd]
  R7 = Resistor [tolerance=±5% resistance=220 package=THT]
  D129 = Rectifier Diode [part_number=1N4004 package="300 mil [THT]"]
  R8 = Resistor [tolerance=±5% resistance=220 package=THT]
  R9 = Resistor [tolerance=±5% resistance=220 package=THT]
  R10 = Resistor [tolerance=±5% resistance=470 package=THT]
  Part4 = Adafruit MPR121
  NEOPIXEL1 = Neopixel Strip -- White (60/m)
  MIDI_OUT = DIN-5 jack (MIDI) [package=THT]
  Pull-Down_Resistors = Resistor [tolerance=±5% resistance=10k package=THT]
  R12 = Resistor [tolerance=±5% resistance=10k package=THT]
  R13 = Resistor [tolerance=±5% resistance=10k package=THT]
  R14 = Resistor [tolerance=±5% resistance=10k package=THT]
  R15 = Resistor [tolerance=±5% resistance=10k package=THT]
  R16 = Resistor [tolerance=±5% resistance=10k package=THT]
  R18 = Resistor [tolerance=±5% resistance=10k package=THT]
  R20 = Resistor [tolerance=±5% resistance=10k package=THT]
  R21 = Resistor [tolerance=±5% resistance=10k package=THT]
  R22 = Resistor [tolerance=±5% resistance=10k package=THT]
  R23 = Resistor [tolerance=±5% resistance=10k package=THT]
  R24 = Resistor [tolerance=±5% resistance=10k package=THT]
  R25 = Resistor [tolerance=±5% resistance=10k package=THT]
  R26 = Resistor [tolerance=±5% resistance=10k package=THT]
  R17 = Resistor [tolerance=±5% resistance=10k package=THT]
  R19 = Resistor [tolerance=±5% resistance=10k package=THT]
  R27 = Resistor [tolerance=±5% resistance=1k package=THT]
  R28 = Resistor [tolerance=±5% resistance=470 package=THT]
  R29 = Resistor [tolerance=±5% resistance=100 package=THT]
  LED1 = LED - 5mm [color="White (6500K)" package="5 mm [THT]"]
  IR_Prox = Infrared Proximity Sensor
  Rot_Pot = Slide Potentiometer [maximum_resistance=7.5kΩ]
  Rot_Pot_2 = Trimmer Potentiometer [maximum_resistance=10kΩ package=THT]
  C3 = Ceramic Capacitor [capacitance=100nF package="100 mil [THT, multilayer]"]
  C2 = Electrolytic Capacitor [capacitance=100µF package="100 mil [THT, electrolytic]"]
  Q1 = MOSFET-NCHANNEL [package=to220v]
  R30 = Resistor [tolerance=±5% resistance=10k package=THT]
  C4 = Ceramic Capacitor [capacitance=100nF package="100 mil [THT, multilayer]"]
  C5 = Ceramic Capacitor [capacitance=100nF package="100 mil [THT, multilayer]"]
  LED2 = LED - 5mm [color="Infrared (850nm)" package="5 mm [THT]"]
  4xIRLED = LED - 5mm [color="Infrared (850nm)" package="5 mm [THT]"]
  LED4 = LED - 5mm [color="Infrared (850nm)" package="5 mm [THT]"]
  LED5 = LED - 5mm [color="Infrared (850nm)" package="5 mm [THT]"]
  R31 = Resistor [tolerance=±5% resistance=100 package=THT]
  R32 = Resistor [tolerance=±5% resistance=47 package=THT]
  Rotary_Encoder = Rotary Encoder [package=THT]
  S65 = Round Pushbutton
  S66 = Round Pushbutton
  3x_Pushbuttons = Round Pushbutton
  RE_Button = Round Pushbutton
  R33 = Resistor [tolerance=±5% resistance=100 package=THT]
  C6 = Ceramic Capacitor [capacitance=100nF package="100 mil [THT, multilayer]"]
  C7 = Ceramic Capacitor [capacitance=100nF package="100 mil [THT, multilayer]"]
  C9 = Ceramic Capacitor [capacitance=100nF package="100 mil [THT, multilayer]"]
  C10 = Ceramic Capacitor [capacitance=100nF package="100 mil [THT, multilayer]"]

nets:
  N1: Part1.A15, Pressure_Sensing_Resistor.pin_1, R2.Pin_1
  N2: Part1.A0, Slide_Pot.wiper, C3.1
  N3: Part1.A1, IR_Prox.Vout
  N4: Part1.A2, Rot_Pot_2.wiper, C7.1
  N5: Part1.A3, Rot_Pot.wiper, C6.1
  N6: Part1.D21/SCL, Part4.SCL
  N7: Part1.D20/SDA, Part4.SDA
  N8: Part1.D19/RX1, 7.VOUT, R10.Pin_1
  N9: Part1.D18/TX1, R7.Pin_0
  GND: Part1.GND, R2.Pin_0, Slide_Pot.leg1, C1.-, Power_plug1.GND, 7.GND, Part4.GND, NEOPIXEL1.GND, MIDI_OUT.2, MIDI_OUT.GND, Pull-Down_Resistors.Pin_0, R12.Pin_0, R13.Pin_0, R14.Pin_0, R15.Pin_0, R16.Pin_0, R18.Pin_0, R20.Pin_0, R21.Pin_0, R22.Pin_0, R23.Pin_0, R24.Pin_0, R25.Pin_0, R26.Pin_0, R17.Pin_0, R19.Pin_0, R27.Pin_1, LED1.cathode, IR_Prox.GND, Rot_Pot.leg1, Rot_Pot_2.leg1, C3.0, C2.-, R30.Pin_1, LED2.cathode, LED4.cathode, LED5.cathode, Rotary_Encoder.EncoderPinC, S65.leg0, S66.leg0, 3x_Pushbuttons.leg0, RE_Button.leg0, C6.0, C7.0, C9.0, C10.0
  N10: Part1.D12_PWM, R29.Pin_1
  N11: Part1.D11_PWM, R31.Pin_1
  N12: Part1.D10_PWM, R32.Pin_1
  N13: Part1.D9_PWM, R33.Pin_1
  N14: Part1.D8_PWM, R28.Pin_0
  VCC: Part1.5V, Pressure_Sensing_Resistor.pin_0, Slide_Pot.leg2, 7.VCC, R8.Pin_0, R10.Pin_0, Part4.VIN, IR_Prox.Vcc, Rot_Pot.leg2, Rot_Pot_2.leg2, C2.+, Q1.D
  N15: Part1.D2_PWM, Rotary_Encoder.EncoderPinB, C9.1
  N16: Part1.D3_PWM, Rotary_Encoder.EncoderPinA, C10.1
  N17: Part1.D4_PWM, RE_Button.leg1
  N18: Part1.D24, J2.pin1, Pull-Down_Resistors.Pin_1
  N19: Part1.D25, J2.pin2, R18.Pin_1
  N20: Part1.D26, J2.pin3, R16.Pin_1
  N21: Part1.D28, J2.pin5, R12.Pin_1
  N22: Part1.D30, J2.pin7, R13.Pin_1
  N23: Part1.D31, J2.pin8
  N24: Part1.D32, J2.pin9, R14.Pin_1
  N25: Part1.D33, J2.pin10
  N26: Part1.D34, J2.pin11, R15.Pin_1
  N27: Part1.D35, J2.pin12
  N28: Part1.D36, J2.pin13, R19.Pin_1
  N29: Part1.D37, J2.pin14
  N30: Part1.D38, J2.pin15, R17.Pin_1
  N31: Part1.D39, J2.pin16
  N32: Part1.D40, J2.pin17, R22.Pin_1
  N33: Part1.D41, J2.pin18
  N34: Part1.D42, J2.pin19, R24.Pin_1
  N35: Part1.D43, J2.pin20
  N36: Part1.D44, J2.pin21, R20.Pin_1
  N37: Part1.D45, J2.pin22
  N38: Part1.D46, J2.pin23, R25.Pin_1
  N39: Part1.D47, J2.pin24, R21.Pin_1
  N40: Part1.D48, J2.pin25, R26.Pin_1
  N41: Part1.D49, J2.pin26, R23.Pin_1
  N42: Part1.D50, S65.leg1
  N43: Part1.D51, S66.leg1
  N44: Part1.D52, 3x_Pushbuttons.leg1
  N45: J3.pin1, D2.cathode, D4.cathode, D6.cathode, D8.cathode, D11.cathode, D12.cathode, D15.cathode, D16.cathode
  N46: J3.pin2, D1.cathode, D3.cathode, D5.cathode, D7.cathode, D9.cathode, D10.cathode, D13.cathode, D14.cathode
  N47: J3.pin3, D18.cathode, D19.cathode, D21.cathode, D23.cathode, D24.cathode, D27.cathode, D28.cathode, D29.cathode
  N48: J3.pin5, D17.cathode, D20.cathode, D22.cathode, D25.cathode, D26.cathode, D30.cathode, D31.cathode, D32.cathode
  N49: J3.pin7, D34.cathode, D36.cathode, D37.cathode, D38.cathode, D39.cathode, D42.cathode, D46.cathode, D59.cathode
  N50: J3.pin8, S9.leg1, S9.leg4, S17.leg1, S17.leg4, S29.leg1, S29.leg4, S33.leg1, S33.leg4, S38.leg1, S38.leg4, S55.leg1, S55.leg4, S56.leg1, S56.leg4, S1.leg1, S1.leg4
  N51: J3.pin9, D33.cathode, D41.cathode, D45.cathode, D54.cathode, D56.cathode, D57.cathode, D61.cathode, D62.cathode
  N52: J3.pin10, S16.leg1, S16.leg4, S23.leg1, S23.leg4, S31.leg1, S31.leg4, S43.leg1, S43.leg4, S47.leg1, S47.leg4, S51.leg1, S51.leg4, S60.leg1, S60.leg4, S2.leg1, S2.leg4
  N53: J3.pin11, D35.cathode, D43.cathode, D44.cathode, D48.cathode, D51.cathode, D60.cathode, D63.cathode, D64.cathode
  N54: J3.pin12, S14.leg1, S14.leg4, S22.leg1, S22.leg4, S26.leg1, S26.leg4, S34.leg1, S34.leg4, S39.leg1, S39.leg4, S48.leg1, S48.leg4, S64.leg1, S64.leg4, S3.leg1, S3.leg4
  N55: J3.pin13, D40.cathode, D47.cathode, D49.cathode, D50.cathode, D52.cathode, D53.cathode, D55.cathode, D58.cathode
  N56: J3.pin14, S10.leg1, S10.leg4, S18.leg1, S18.leg4, S25.leg1, S25.leg4, S37.leg1, S37.leg4, S42.leg1, S42.leg4, S50.leg1, S50.leg4, S54.leg1, S54.leg4, S4.leg1, S4.leg4
  N57: J3.pin15, D69.cathode, D87.cathode, D111.cathode, D112.cathode, D121.cathode, D126.cathode, D127.cathode, D128.cathode
  N58: J3.pin16, S12.leg1, S12.leg4, S28.leg1, S28.leg4, S32.leg1, S32.leg4, S36.leg1, S36.leg4, S40.leg1, S40.leg4, S44.leg1, S44.leg4, S63.leg1, S63.leg4, S5.leg1, S5.leg4
  N59: J3.pin17, D65.cathode, D75.cathode, D86.cathode, D88.cathode, D95.cathode, D96.cathode, D103.cathode, D124.cathode
  N60: J3.pin18, S13.leg1, S13.leg4, S19.leg1, S19.leg4, S30.leg1, S30.leg4, S52.leg1, S52.leg4, S58.leg1, S58.leg4, S61.leg1, S61.leg4, S7.leg1, S7.leg4
  N61: J3.pin19, D66.cathode, D68.cathode, D70.cathode, D80.cathode, D100.cathode, D102.cathode, D114.cathode, D120.cathode
  N62: J3.pin20, S15.leg1, S15.leg4, S21.leg1, S21.leg4, S27.leg1, S27.leg4, S49.leg1, S49.leg4, S57.leg1, S57.leg4, S62.leg1, S62.leg4, S6.leg1, S6.leg4
  N63: J3.pin21, D67.cathode, D81.cathode, D91.cathode, D108.cathode, D115.cathode, D116.cathode, D118.cathode, D125.cathode
  N64: J3.pin22, S11.leg1, S11.leg4, S20.leg1, S20.leg4, S24.leg1, S24.leg4, S46.leg1, S46.leg4, S53.leg1, S53.leg4, S59.leg1, S59.leg4, S8.leg1, S8.leg4
  N65: J3.pin23, D78.cathode, D84.cathode, D85.cathode, D89.cathode, D90.cathode, D105.cathode, D107.cathode, D117.cathode
  N66: J3.pin24, D77.cathode, D79.cathode, D82.cathode, D83.cathode, D94.cathode
  N67: J3.pin25, D71.cathode, D73.cathode, D74.cathode, D97.cathode, D110.cathode, D113.cathode, D119.cathode, D122.cathode
  N68: J3.pin26, D76.cathode, D92.cathode, D98.cathode, D99.cathode, D106.cathode
  N69: D1.anode, S1.leg3
  N70: D2.anode, S1.leg0
  N71: D3.anode, S2.leg3
  N72: D4.anode, S2.leg0
  N73: D5.anode, S3.leg3
  N74: D6.anode, S3.leg0
  N75: D7.anode, S4.leg3
  N76: D8.anode, S4.leg0
  N77: D9.anode, S5.leg3
  N78: D10.anode, S6.leg3
  N79: D11.anode, S5.leg0
  N80: D12.anode, S7.leg0
  N81: D13.anode, S8.leg3
  N82: D14.anode, S7.leg3
  N83: D15.anode, S8.leg0
  N84: D16.anode, S6.leg0
  N85: D17.anode, S9.leg0
  N86: D18.anode, S11.leg3
  N87: D19.anode, S10.leg3
  N88: D20.anode, S14.leg0
  N89: D21.anode, S16.leg3
  N90: D22.anode, S16.leg0
  N91: D23.anode, S14.leg3
  N92: D24.anode, S13.leg3
  N93: D25.anode, S10.leg0
  N94: D26.anode, S15.leg0
  N95: D27.anode, S12.leg3
  N96: D28.anode, S15.leg3
  N97: D29.anode, S9.leg3
  N98: D30.anode, S12.leg0
  N99: D31.anode, S13.leg0
  N100: D32.anode, S11.leg0
  N101: D33.anode, S17.leg0
  N102: D34.anode, S26.leg3
  N103: D35.anode, S32.leg3
  N104: D36.anode, S20.leg3
  N105: D37.anode, S28.leg3
  N106: D38.anode, S21.leg3
  N107: D39.anode, S17.leg3
  N108: D40.anode, S22.leg0
  N109: D41.anode, S21.leg0
  N110: D42.anode, S25.leg3
  N111: D43.anode, S24.leg3
  N112: D44.anode, S27.leg3
  N113: D45.anode, S20.leg0
  N114: D46.anode, S19.leg3
  N115: D47.anode, S24.leg0
  N116: D48.anode, S30.leg3
  N117: D49.anode, S27.leg0
  N118: D50.anode, S29.leg0
  N119: D51.anode, S23.leg3
  N120: D52.anode, S23.leg0
  N121: D53.anode, S30.leg0
  N122: D54.anode, S28.leg0
  N123: D55.anode, S32.leg0
  N124: D56.anode, S25.leg0
  N125: D57.anode, S26.leg0
  N126: D58.anode, S18.leg0
  N127: D59.anode, S31.leg3
  N128: D60.anode, S18.leg3
  N129: D61.anode, S31.leg0
  N130: D62.anode, S19.leg0
  N131: D63.anode, S29.leg3
  N132: D64.anode, S22.leg3
  N133: D65.anode, S33.leg0
  N134: D66.anode, S61.leg3
  N135: D67.anode, S50.leg0
  N136: D68.anode, S50.leg3
  N137: D69.anode, S57.leg3
  N138: D70.anode, S64.leg3
  N139: D71.anode, S54.leg0
  N140: D73.anode, S60.leg0
  N141: D74.anode, S38.leg0
  N142: D75.anode, S58.leg0
  N143: D76.anode, S56.leg3
  N144: D77.anode, S42.leg0
  N145: D78.anode, S53.leg3
  N146: D79.anode, S48.leg0
  N147: D80.anode, S46.leg3
  N148: D81.anode, S64.leg0
  N149: D82.anode, S43.leg0
  N150: D83.anode, S56.leg0
  N151: D84.anode, S52.leg3
  N152: D85.anode, S49.leg3
  N153: D86.anode, S63.leg0
  N154: D87.anode, S58.leg3
  N155: D88.anode, S37.leg0
  N156: D89.anode, S39.leg3
  N157: D90.anode, S54.leg3
  N158: D91.anode, S46.leg0
  N159: D92.anode, S42.leg3
  N160: D94.anode, S44.leg0
  N161: D95.anode, S47.leg0
  N162: D96.anode, S34.leg0
  N163: D97.anode, S40.leg0
  N164: D98.anode, S48.leg3
  N165: D99.anode, S43.leg3
  N166: D100.anode, S36.leg3
  N167: D102.anode, S62.leg3
  N168: D103.anode, S57.leg0
  N169: D105.anode, S38.leg3
  N170: D106.anode, S44.leg3
  N171: D107.anode, S40.leg3
  N172: D108.anode, S61.leg0
  N173: D110.anode, S39.leg0
  N174: D111.anode, S59.leg3
  N175: D112.anode, S34.leg3
  N176: D113.anode, S52.leg0
  N177: D114.anode, S51.leg3
  N178: D115.anode, S55.leg0
  N179: D116.anode, S51.leg0
  N180: D117.anode, S60.leg3
  N181: D118.anode, S62.leg0
  N182: D119.anode, S53.leg0
  N183: D120.anode, S55.leg3
  N184: D121.anode, S47.leg3
  N185: D122.anode, S49.leg0
  N186: D124.anode, S59.leg0
  N187: D125.anode, S36.leg0
  N188: D126.anode, S63.leg3
  N189: D127.anode, S33.leg3
  N190: D128.anode, S37.leg3
  VCC_2: C1.+, Power_plug1.VCC, NEOPIXEL1.+5V
  N191: MIDI_IN.5, 7.C, D129.anode
  N192: MIDI_IN.4, R9.Pin_0
  N193: 7.A, D129.cathode, R9.Pin_1
  N194: R7.Pin_1, MIDI_OUT.5
  N195: R8.Pin_1, MIDI_OUT.4
  N196: Part4.ELEC11, Q1.G, C4.0
  N197: NEOPIXEL1.DI, R28.Pin_1
  N198: R29.Pin_0, LED1.anode
  N199: Q1.S, R30.Pin_0, C5.1
  N200: LED2.anode, 4xIRLED.cathode
  N201: 4xIRLED.anode, R32.Pin_0
  N202: LED4.anode, R33.Pin_0
  N203: LED5.anode, R31.Pin_0

notes:
  MK3
  KD0
  KD1
  KD2
  KD3
  KD4
  KD7
  KD6
  KD5
  BR3
  MK4
  BR4
  MK5
  BR5
  MK6
  BR6
  MK10
  BR10
  BR7
  MK7
  BR8
  MK8
  BR9
  MK9
  1m strip of 60 RGB Pixels
  5V 8A LED Power Supply
  Shielded Cap Sensor

custom parts:
  Pushbutton: A generic pushbutton.
  Adafruit MPR121: Add lots of touch sensors to your next microcontroller project with this easy-to-use 12-channel capacitive touch sensor breakout board, starring the MPR121. This chip can handle up to 12 individual touch pads. The MPR121 has support for only I2C, which can be implemented with nearly any microcontroller. You can select one of 4 addresses with the ADDR pin, for a total of 48 capacitive touch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
  Neopixel Strip -- White (60/m): Neopixel Strip, White, 60 pixels per meter.
