# Fritzing sketch Optical Synthesizer (saved by Fritzing 0.9.3b)
breadboards: 1

parts:
  Part1 = Arduino Mega 2560 (Rev3)
  J2 = shrouded pin header, 26 pins [form="♂ (shrouded male)"]
  J3 = double row female pin header, 26 pins [form="♀ (female)"]
  Pressure_Sensing_Resistor = Basic Force Sensing Resistor (FSR) [package=THT]
  D1 = P1000K [part_number=P1000K]
  D2 = P1000K [part_number=P1000K]
  D3 = P1000K [part_number=P1000K]
  D4 = P1000K [part_number=P1000K]
  D5 = P1000K [part_number=P1000K]
  D6 = P1000K [part_number=P1000K]
  D7 = P1000K [part_number=P1000K]
  D8 = P1000K [part_number=P1000K]
  D9 = P1000K [part_number=P1000K]
  D10 = P1000K [part_number=P1000K]
  D11 = P1000K [part_number=P1000K]
  D12 = P1000K [part_number=P1000K]
  D13 = P1000K [part_number=P1000K]
  D14 = P1000K [part_number=P1000K]
  D15 = P1000K [part_number=P1000K]
  D16 = P1000K [part_number=P1000K]
  D17 = P1000K [part_number=P1000K]
  D18 = P1000K [part_number=P1000K]
  D19 = P1000K [part_number=P1000K]
  D20 = P1000K [part_number=P1000K]
  D21 = P1000K [part_number=P1000K]
  D22 = P1000K [part_number=P1000K]
  D23 = P1000K [part_number=P1000K]
  D24 = P1000K [part_number=P1000K]
  D25 = P1000K [part_number=P1000K]
  D26 = P1000K [part_number=P1000K]
  D27 = P1000K [part_number=P1000K]
  D28 = P1000K [part_number=P1000K]
  D29 = P1000K [part_number=P1000K]
  D30 = P1000K [part_number=P1000K]
  D31 = P1000K [part_number=P1000K]
  D32 = P1000K [part_number=P1000K]
  S9 = Pushbutton [package=THT]
  S10 = Pushbutton [package=THT]
  S11 = Pushbutton [package=THT]
  S12 = Pushbutton [package=THT]
  S13 = Pushbutton [package=THT]
  S14 = Pushbutton [package=THT]
  S15 = Pushbutton [package=THT]
  S16 = Pushbutton [package=THT]
  D33 = P1000K [part_number=P1000K]
  D34 = P1000K [part_number=P1000K]
  D35 = P1000K [part_number=P1000K]
  D36 = P1000K [part_number=P1000K]
  D37 = P1000K [part_number=P1000K]
  D38 = P1000K [part_number=P1000K]
  D39 = P1000K [part_number=P1000K]
  D40 = P1000K [part_number=P1000K]
  D41 = P1000K [part_number=P1000K]
  D42 = P1000K [part_number=P1000K]
  D43 = P1000K [part_number=P1000K]
  D44 = P1000K [part_number=P1000K]
  D45 = P1000K [part_number=P1000K]
  D46 = P1000K [part_number=P1000K]
  D47 = P1000K [part_number=P1000K]
  D48 = P1000K [part_number=P1000K]
  D49 = P1000K [part_number=P1000K]
  D50 = P1000K [part_number=P1000K]
  D51 = P1000K [part_number=P1000K]
  D52 = P1000K [part_number=P1000K]
  D53 = P1000K [part_number=P1000K]
  D54 = P1000K [part_number=P1000K]
  D55 = P1000K [part_number=P1000K]
  D56 = P1000K [part_number=P1000K]
  D57 = P1000K [part_number=P1000K]
  D58 = P1000K [part_number=P1000K]
  D59 = P1000K [part_number=P1000K]
  D60 = P1000K [part_number=P1000K]
  D61 = P1000K [part_number=P1000K]
  D62 = P1000K [part_number=P1000K]
  D63 = P1000K [part_number=P1000K]
  D64 = P1000K [part_number=P1000K]
  S17 = Pushbutton [package=THT]
  S18 = Pushbutton [package=THT]
  S19 = Pushbutton [package=THT]
  S20 = Pushbutton [package=THT]
  S21 = Pushbutton [package=THT]
  S22 = Pushbutton [package=THT]
  S23 = Pushbutton [package=THT]
  S24 = Pushbutton [package=THT]
  S25 = Pushbutton [package=THT]
  S26 = Pushbutton [package=THT]
  S27 = Pushbutton [package=THT]
  S28 = Pushbutton [package=THT]
  S29 = Pushbutton [package=THT]
  S30 = Pushbutton [package=THT]
  S31 = Pushbutton [package=THT]
  S32 = Pushbutton [package=THT]
  D65 = P1000K [part_number=P1000K]
  D66 = P1000K [part_number=P1000K]
  D67 = P1000K [part_number=P1000K]
  D68 = P1000K [part_number=P1000K]
  D69 = P1000K [part_number=P1000K]
  D70 = P1000K [part_number=P1000K]
  D71 = P1000K [part_number=P1000K]
  D73 = P1000K [part_number=P1000K]
  D74 = P1000K [part_number=P1000K]
  D75 = P1000K [part_number=P1000K]
  D76 = P1000K [part_number=P1000K]
  D77 = P1000K [part_number=P1000K]
  D78 = P1000K [part_number=P1000K]
  D79 = P1000K [part_number=P1000K]
  D80 = P1000K [part_number=P1000K]
  D81 = P1000K [part_number=P1000K]
  D82 = P1000K [part_number=P1000K]
  D83 = P1000K [part_number=P1000K]
  D84 = P1000K [part_number=P1000K]
  D85 = P1000K [part_number=P1000K]
  D86 = P1000K [part_number=P1000K]
  D87 = P1000K [part_number=P1000K]
  D88 = P1000K [part_number=P1000K]
  D89 = P1000K [part_number=P1000K]
  D90 = P1000K [part_number=P1000K]
  D91 = P1000K [part_number=P1000K]
  D92 = P1000K [part_number=P1000K]
  D94 = P1000K [part_number=P1000K]
  D95 = P1000K [part_number=P1000K]
  D96 = P1000K [part_number=P1000K]
  D97 = P1000K [part_number=P1000K]
  D98 = P1000K [part_number=P1000K]
  D99 = P1000K [part_number=P1000K]
  D100 = P1000K [part_number=P1000K]
  D102 = P1000K [part_number=P1000K]
  D103 = P1000K [part_number=P1000K]
  D105 = P1000K [part_number=P1000K]
  D106 = P1000K [part_number=P1000K]
  D107 = P1000K [part_number=P1000K]
  D108 = P1000K [part_number=P1000K]
  D110 = P1000K [part_number=P1000K]
  D111 = P1000K [part_number=P1000K]
  D112 = P1000K [part_number=P1000K]
  D113 = P1000K [part_number=P1000K]
  D114 = P1000K [part_number=P1000K]
  D115 = P1000K [part_number=P1000K]
  D116 = P1000K [part_number=P1000K]
  D117 = P1000K [part_number=P1000K]
  D118 = P1000K [part_number=P1000K]
  D119 = P1000K [part_number=P1000K]
  D120 = P1000K [part_number=P1000K]
  D121 = P1000K [part_number=P1000K]
  D122 = P1000K [part_number=P1000K]
  D124 = P1000K [part_number=P1000K]
  D125 = P1000K [part_number=P1000K]
  D126 = P1000K [part_number=P1000K]
  D127 = P1000K [part_number=P1000K]
  D128 = P1000K [part_number=P1000K]
  S33 = Pushbutton [package=THT]
  S34 = Pushbutton [package=THT]
  S36 = Pushbutton [package=THT]
  S37 = Pushbutton [package=THT]
  S38 = Pushbutton [package=THT]
  S39 = Pushbutton [package=THT]
  S40 = Pushbutton [package=THT]
  S42 = Pushbutton [package=THT]
  S43 = Pushbutton [package=THT]
  S44 = Pushbutton [package=THT]
  S46 = Pushbutton [package=THT]
  S47 = Pushbutton [package=THT]
  S48 = Pushbutton [package=THT]
  S49 = Pushbutton [package=THT]
  S50 = Pushbutton [package=THT]
  S51 = Pushbutton [package=THT]
  S52 = Pushbutton [package=THT]
  S53 = Pushbutton [package=THT]
  S54 = Pushbutton [package=THT]
  S55 = Pushbutton [package=THT]
  S56 = Pushbutton [package=THT]
  S57 = Pushbutton [package=THT]
  S58 = Pushbutton [package=THT]
  S59 = Pushbutton [package=THT]
  S60 = Pushbutton [package=THT]
  S61 = Pushbutton [package=THT]
  S62 = Pushbutton [package=THT]
  S63 = Pushbutton [package=THT]
  S64 = Pushbutton [package=THT]
  S7 = Pushbutton [package=THT]
  S6 = Pushbutton [package=THT]
  S1 = Pushbutton [package=THT]
  S8 = Pushbutton [package=THT]
  S2 = Pushbutton [package=THT]
  S5 = Pushbutton [package=THT]
  S4 = Pushbutton [package=THT]
  S3 = Pushbutton [package=THT]
  R2 = Resistor [tolerance=±5% resistance=220 package=THT]

nets:
  N1: Part1.A0, Pressure_Sensing_Resistor.pin_1, R2.Pin_1
  GND: Part1.GND, R2.Pin_0
  N2: Part1.5V, Pressure_Sensing_Resistor.pin_0
  N3: Part1.D22, J2.pin1
  N4: Part1.D23, J2.pin2
  N5: Part1.D24, J2.pin3
  N6: Part1.D26, J2.pin5
  N7: Part1.D28, J2.pin7
  N8: Part1.D29, J2.pin8
  N9: Part1.D30, J2.pin9
  N10: Part1.D31, J2.pin10
  N11: Part1.D32, J2.pin11
  N12: Part1.D33, J2.pin12
  N13: Part1.D34, J2.pin13
  N14: Part1.D35, J2.pin14
  N15: Part1.D36, J2.pin15
  N16: Part1.D37, J2.pin16
  N17: Part1.D38, J2.pin17
  N18: Part1.D39, J2.pin18
  N19: Part1.D40, J2.pin19
  N20: Part1.D41, J2.pin20
  N21: Part1.D42, J2.pin21
  N22: Part1.D43, J2.pin22
  N23: Part1.D44, J2.pin23
  N24: Part1.D45, J2.pin24
  N25: Part1.D46, J2.pin25
  N26: Part1.D47, J2.pin26
  N27: J3.pin1, D2.cathode, D4.cathode, D6.cathode, D8.cathode, D11.cathode, D12.cathode, D15.cathode, D16.cathode
  N28: J3.pin2, D1.cathode, D3.cathode, D5.cathode, D7.cathode, D9.cathode, D10.cathode, D13.cathode, D14.cathode
  N29: J3.pin3, D18.cathode, D19.cathode, D21.cathode, D23.cathode, D24.cathode, D27.cathode, D28.cathode, D29.cathode
  N30: J3.pin5, D17.cathode, D20.cathode, D22.cathode, D25.cathode, D26.cathode, D30.cathode, D31.cathode, D32.cathode
  N31: J3.pin7, D34.cathode, D36.cathode, D37.cathode, D38.cathode, D39.cathode, D42.cathode, D46.cathode, D59.cathode
  N32: J3.pin8, S9.leg1, S9.leg4, S1.leg1, S1.leg4
  N33: J3.pin9, D33.cathode, D41.cathode, D45.cathode, D54.cathode, D56.cathode, D57.cathode, D61.cathode, D62.cathode
  N34: J3.pin10, S16.leg1, S16.leg4, S2.leg1, S2.leg4
  N35: J3.pin11, D35.cathode, D43.cathode, D44.cathode, D48.cathode, D51.cathode, D60.cathode, D63.cathode, D64.cathode
  N36: J3.pin12, S14.leg1, S14.leg4, S3.leg1, S3.leg4
  N37: J3.pin13, D40.cathode, D47.cathode, D49.cathode, D50.cathode, D52.cathode, D53.cathode, D55.cathode, D58.cathode
  N38: J3.pin14, S10.leg1, S10.leg4, S4.leg1, S4.leg4
  N39: J3.pin15, D127.cathode
  N40: J3.pin16, S12.leg1, S12.leg4, S5.leg1, S5.leg4
  N41: J3.pin17, D65.cathode
  N42: J3.pin18, S13.leg1, S13.leg4, S7.leg1, S7.leg4
  N43: J3.pin19, D120.cathode
  N44: J3.pin20, S15.leg1, S15.leg4, S6.leg1, S6.leg4
  N45: J3.pin21, D115.cathode
  N46: J3.pin22, S11.leg1, S11.leg4, S8.leg1, S8.leg4
  N47: J3.pin23, D105.cathode
  N48: J3.pin24, D77.cathode, D79.cathode, D82.cathode, D83.cathode, D94.cathode
  N49: J3.pin25, D74.cathode
  N50: J3.pin26, D76.cathode, D92.cathode, D98.cathode, D99.cathode, D106.cathode
  N51: D1.anode, S1.leg3
  N52: D2.anode, S1.leg0
  N53: D3.anode, S2.leg3
  N54: D4.anode, S2.leg0
  N55: D5.anode, S3.leg3
  N56: D6.anode, S3.leg0
  N57: D7.anode, S4.leg3
  N58: D8.anode, S4.leg0
  N59: D9.anode, S5.leg3
  N60: D10.anode, S6.leg3
  N61: D11.anode, S5.leg0
  N62: D12.anode, S7.leg0
  N63: D13.anode, S8.leg3
  N64: D14.anode, S7.leg3
  N65: D15.anode, S8.leg0
  N66: D16.anode, S6.leg0
  N67: D17.anode, S9.leg0
  N68: D18.anode, S11.leg3
  N69: D19.anode, S10.leg3
  N70: D20.anode, S14.leg0
  N71: D21.anode, S16.leg3
  N72: D22.anode, S16.leg0
  N73: D23.anode, S14.leg3
  N74: D24.anode, S13.leg3
  N75: D25.anode, S10.leg0
  N76: D26.anode, S15.leg0
  N77: D27.anode, S12.leg3
  N78: D28.anode, S15.leg3
  N79: D29.anode, S9.leg3
  N80: D30.anode, S12.leg0
  N81: D31.anode, S13.leg0
  N82: D32.anode, S11.leg0
  N83: D33.anode, S17.leg0
  N84: D34.anode, S26.leg3
  N85: D35.anode, S32.leg3
  N86: D36.anode, S20.leg3
  N87: D37.anode, S28.leg3
  N88: D38.anode, S21.leg3
  N89: D39.anode, S17.leg3
  N90: D40.anode, S22.leg0
  N91: D41.anode, S21.leg0
  N92: D42.anode, S25.leg3
  N93: D43.anode, S24.leg3
  N94: D44.anode, S27.leg3
  N95: D45.anode, S20.leg0
  N96: D46.anode, S19.leg3
  N97: D47.anode, S24.leg0
  N98: D48.anode, S30.leg3
  N99: D49.anode, S27.leg0
  N100: D50.anode, S29.leg0
  N101: D51.anode, S23.leg3
  N102: D52.anode, S23.leg0
  N103: D53.anode, S30.leg0
  N104: D54.anode, S28.leg0
  N105: D55.anode, S32.leg0
  N106: D56.anode, S25.leg0
  N107: D57.anode, S26.leg0
  N108: D58.anode, S18.leg0
  N109: D59.anode, S31.leg3
  N110: D60.anode, S18.leg3
  N111: D61.anode, S31.leg0
  N112: D62.anode, S19.leg0
  N113: D63.anode, S29.leg3
  N114: D64.anode, S22.leg3
  N115: S17.leg1, S17.leg4
  N116: S18.leg1, S18.leg4
  N117: S19.leg1, S19.leg4
  N118: S20.leg1, S20.leg4
  N119: S21.leg1, S21.leg4
  N120: S22.leg1, S22.leg4
  N121: S23.leg1, S23.leg4
  N122: S24.leg1, S24.leg4
  N123: S25.leg1, S25.leg4
  N124: S26.leg1, S26.leg4
  N125: S27.leg1, S27.leg4
  N126: S28.leg1, S28.leg4
  N127: S29.leg1, S29.leg4
  N128: S30.leg1, S30.leg4
  N129: S31.leg1, S31.leg4
  N130: S32.leg1, S32.leg4
  N131: D65.anode, S33.leg0
  N132: D66.anode, S61.leg3
  N133: D67.anode, S50.leg0
  N134: D68.anode, S50.leg3
  N135: D69.anode, S57.leg3
  N136: D70.anode, S64.leg3
  N137: D71.anode, S54.leg0
  N138: D73.anode, S60.leg0
  N139: D74.anode, S38.leg0
  N140: D75.anode, S58.leg0
  N141: D76.anode, S56.leg3
  N142: D77.anode, S42.leg0
  N143: D78.anode, S53.leg3
  N144: D79.anode, S48.leg0
  N145: D80.anode, S46.leg3
  N146: D81.anode, S64.leg0
  N147: D82.anode, S43.leg0
  N148: D83.anode, S56.leg0
  N149: D84.anode, S52.leg3
  N150: D85.anode, S49.leg3
  N151: D86.anode, S63.leg0
  N152: D87.anode, S58.leg3
  N153: D88.anode, S37.leg0
  N154: D89.anode, S39.leg3
  N155: D90.anode, S54.leg3
  N156: D91.anode, S46.leg0
  N157: D92.anode, S42.leg3
  N158: D94.anode, S44.leg0
  N159: D95.anode, S47.leg0
  N160: D96.anode, S34.leg0
  N161: D97.anode, S40.leg0
  N162: D98.anode, S48.leg3
  N163: D99.anode, S43.leg3
  N164: D100.anode, S36.leg3
  N165: D102.anode, S62.leg3
  N166: D103.anode, S57.leg0
  N167: D105.anode, S38.leg3
  N168: D106.anode, S44.leg3
  N169: D107.anode, S40.leg3
  N170: D108.anode, S61.leg0
  N171: D110.anode, S39.leg0
  N172: D111.anode, S59.leg3
  N173: D112.anode, S34.leg3
  N174: D113.anode, S52.leg0
  N175: D114.anode, S51.leg3
  N176: D115.anode, S55.leg0
  N177: D116.anode, S51.leg0
  N178: D117.anode, S60.leg3
  N179: D118.anode, S62.leg0
  N180: D119.anode, S53.leg0
  N181: D120.anode, S55.leg3
  N182: D121.anode, S47.leg3
  N183: D122.anode, S49.leg0
  N184: D124.anode, S59.leg0
  N185: D125.anode, S36.leg0
  N186: D126.anode, S63.leg3
  N187: D127.anode, S33.leg3
  N188: D128.anode, S37.leg3
  N189: S33.leg1, S33.leg4
  N190: S34.leg1, S34.leg4
  N191: S36.leg1, S36.leg4
  N192: S37.leg1, S37.leg4
  N193: S38.leg1, S38.leg4
  N194: S39.leg1, S39.leg4
  N195: S40.leg1, S40.leg4
  N196: S42.leg1, S42.leg4
  N197: S43.leg1, S43.leg4
  N198: S44.leg1, S44.leg4
  N199: S46.leg1, S46.leg4
  N200: S47.leg1, S47.leg4
  N201: S48.leg1, S48.leg4
  N202: S49.leg1, S49.leg4
  N203: S50.leg1, S50.leg4
  N204: S51.leg1, S51.leg4
  N205: S52.leg1, S52.leg4
  N206: S53.leg1, S53.leg4
  N207: S54.leg1, S54.leg4
  N208: S55.leg1, S55.leg4
  N209: S56.leg1, S56.leg4
  N210: S57.leg1, S57.leg4
  N211: S58.leg1, S58.leg4
  N212: S59.leg1, S59.leg4
  N213: S60.leg1, S60.leg4
  N214: S61.leg1, S61.leg4
  N215: S62.leg1, S62.leg4
  N216: S63.leg1, S63.leg4
  N217: S64.leg1, S64.leg4

notes:
  keyboard uses 24 digital I/O ports, D29-D53
  4-10 digital outputs to oscillators
  1 analog signal input from synthesizer, possibly more from potentiometers and sensors.
  Serial/Wi-Fi/Bluetooth data output to Unity
  ??? Outputs to LED array or VGA monitor
  Total I/O = 30+
  MK3
  KD0
  KD1
  KD2
  KD3
  KD4
  KD7
  KD6
  KD5
  BR3
  MK4
  BR4
  MK5
  BR5
  MK6
  BR6
  MK10
  BR10

custom parts:
  Pushbutton: A generic pushbutton.
